// Logisim project RETRON-PROTO-FINAL.circ as structural Verilog: 9 circuits, main circuit main
module main (
  input  in_1,
  input  in_2,
  input  in_3,
  input  in_4,
  output out_5,
  output out_6,
  output out_7,
  output out_8,
  output [7:0] out_9,
  output out_10,
  output [7:0] out_11,
  output out_12,
  output [7:0] out_13,
  output [7:0] out_14,
  output out_15,
  output [7:0] out_16,
  output [7:0] out_17,
  output [7:0] out_18,
  output [7:0] out_19,
  output [7:0] out_20
);

  wire A_ACC, A_ALU, A_MEM, A_MEM_L, A_MEM_U, A_NULL, A_X, A_Y, ALL_FLAGS, ALT_MEM, ALU_AB, ALU_ADD,
       ALU_CARRY, ALU_M, ALU_SUB, ALU_ZERO, and_2_out, and_3_out, and_4_out, and_5_out, and_6_out, and_7_out,
       and_8_out, and_9_out, and_10_out, and_11_out, and_12_out, and_13_out, and_14_out, and_15_out,
       and_16_out, and_17_out, and_24_out, and_25_out, and_26_out, and_27_out, and_28_out, and_29_out,
       and_30_out, and_31_out, and_32_out, and_33_out, and_38_out, and_39_out, and_40_out, and_41_out,
       and_42_out, and_43_out, and_44_out, and_45_out, and_46_out, and_47_out, and_48_out, and_53_out,
       and_54_out, and_55_out, and_56_out, and_57_out, and_58_out, and_59_out, and_60_out, CF_EN, CLK, D_ACC,
       D_ALU, D_FL_CARRY, D_FL_EC, D_FL_I, D_FL_OF, D_FL_SIGN, D_FL_ZC, D_FLAGS, D_L_PCO, D_MEM_L, D_MEM_U,
       D_U_PCO, D_X, D_Y, DEC_STACK, FL_CARRY, FL_EC, FL_I, FL_OF, FL_ZC, INC_STACK, INTERRUPT, INV_FLAG,
       MEM_EN, MEM_W, MEM_WR, n74112_1_nq1, n74112_1_nq2, n74112_2_nq1, n74112_2_nq2, n74112_3_nq1,
       n74112_3_nq2, n74112_4_nq1, n74112_4_nq2, n74137_1_ny1, n74137_1_ny2, n74137_1_ny3, n74137_1_ny4,
       n74137_1_ny5, n74137_1_ny6, n74137_1_ny7, n74137_2_ny0, n74137_2_ny2, n74137_2_ny4, n74137_2_ny5,
       n74137_3_ny6, n74137_3_ny7, n74137_4_ny4, n74137_4_ny5, n74137_4_ny6, n74137_4_ny7, n74137_6_ny0,
       n74137_6_ny1, n74163_2_rco, n74163_3_rco, n74163_4_rco, n74181_1_a_b, n74181_1_cn_4, n74181_2_a_b,
       n74181_2_cn_4, n74193_1_ntcd, n74193_1_ntcu, n74245_3_b2, n74245_3_b3, n74245_3_b5, nand_1_out,
       nFL_CARRY, nFL_EC, nFL_I, nFL_OF, nFL_ZC, nor_1_out, not_1_out, not_2_out, not_5_out, not_6_out,
       not_7_out, not_8_out, not_9_out, not_10_out, not_11_out, not_12_out, not_13_out, not_33_out,
       not_34_out, not_35_out, not_36_out, not_37_out, not_38_out, not_39_out, not_40_out, not_41_out,
       not_42_out, not_43_out, not_44_out, not_46_out, not_47_out, not_48_out, not_49_out, not_50_out,
       not_51_out, not_54_out, not_55_out, not_56_out, not_57_out, nROM_DISABLE, nX, or_1_out, or_3_out,
       PC_CLK, PC_CLK1, PC_CLR, PC_GLOB, PC_LOAD, PC_OE, PC_OE_ALT, PC_OE_STACK, S_ACC, S_ALU, S_FLAGS,
       S_MEM_L, S_MEM_U, S_MEZZ, S_PC_L, S_PC_U, S_SP_H, S_X, S_Y, SET_FLAG, SIC_INHIBIT, SIC_RST, WR_STACK,
       X, xnor_2_out, xnor_3_out, xor_1_out, xor_2_out, xor_3_out, xor_4_out;
  wire [1:0] rom_3_data;
  wire [2:0] CF_RAW;
  wire [3:0] ALU_BUS, ALU_SEL, MEM_BUS, REG_SET;
  wire [6:6] rom_1_data;
  wire [7:0] A_MEM_L_OUT, ACC_IN, MEM_DIRECT, MEZZ_OUT, NULL_MON, PC_RAW_L, PC_RAW_U, PC_REG_L_MON,
       PC_REG_L_OUT, PC_REG_U_MON, PC_REG_U_OUT, SP_H_MON, SP_H_OUT;
  wire [15:0] PC_OUT;

  Clock clock_1 (.out(CLK));
  _74574 u_74574_1 (
    .MONITOR_OUT(out_17), .CLK(S_ACC), ._0Q(ACC_IN[0]), ._1Q(ACC_IN[1]), ._2Q(ACC_IN[2]), ._3Q(ACC_IN[3]),
    ._4Q(ACC_IN[4]), ._5Q(ACC_IN[5]), ._6Q(ACC_IN[6]), ._7Q(ACC_IN[7]), .EN(D_ACC), ._0D(ACC_IN[0]),
    ._1D(ACC_IN[1]), ._2D(ACC_IN[2]), ._3D(ACC_IN[3]), ._4D(ACC_IN[4]), ._5D(ACC_IN[5]), ._6D(ACC_IN[6]),
    ._7D(ACC_IN[7]));
  _74574 u_74574_2 (
    .MONITOR_OUT(out_17), .CLK(S_ACC), ._0Q(A_MEM_L_OUT[0]), ._1Q(A_MEM_L_OUT[1]), ._2Q(A_MEM_L_OUT[2]),
    ._3Q(A_MEM_L_OUT[3]), ._4Q(A_MEM_L_OUT[4]), ._5Q(A_MEM_L_OUT[5]), ._6Q(A_MEM_L_OUT[6]),
    ._7Q(A_MEM_L_OUT[7]), .EN(A_ACC), ._0D(ACC_IN[0]), ._1D(ACC_IN[1]), ._2D(ACC_IN[2]), ._3D(ACC_IN[3]),
    ._4D(ACC_IN[4]), ._5D(ACC_IN[5]), ._6D(ACC_IN[6]), ._7D(ACC_IN[7]));
  _74574 u_74574_3 (
    .MONITOR_OUT(PC_REG_L_MON), .CLK(S_PC_L), ._0Q(PC_REG_L_OUT[0]), ._1Q(PC_REG_L_OUT[1]),
    ._2Q(PC_REG_L_OUT[2]), ._3Q(PC_REG_L_OUT[3]), ._4Q(PC_REG_L_OUT[4]), ._5Q(PC_REG_L_OUT[5]),
    ._6Q(PC_REG_L_OUT[6]), ._7Q(PC_REG_L_OUT[7]), .EN(1'b0), ._0D(ACC_IN[0]), ._1D(ACC_IN[1]),
    ._2D(ACC_IN[2]), ._3D(ACC_IN[3]), ._4D(ACC_IN[4]), ._5D(ACC_IN[5]), ._6D(ACC_IN[6]), ._7D(ACC_IN[7]));
  ROM #(.addrWidth(11)) rom_1 (
    .addr({CF_RAW, MEZZ_OUT}), .data({INV_FLAG, rom_1_data[6], SIC_RST, PC_CLK, REG_SET}), .sel(not_1_out));
  ROM #(.addrWidth(11)) rom_2 (.addr({CF_RAW, MEZZ_OUT}), .data({MEM_BUS, ALU_BUS}), .sel(not_1_out));
  ROM #(.addrWidth(11)) rom_3 (
    .addr({CF_RAW, MEZZ_OUT}), .data({ALU_SEL, SET_FLAG, ALU_M, rom_3_data}), .sel(not_1_out));
  not not_1 (not_1_out, in_1);
  _74163 u_74163_1 (
    .nLOAD(1'b1), .D0(1'b0), .D1(1'b0), .CLK(CLK), .D2(1'b0), .D3(1'b0), .nCLR(not_2_out), .ENP(1'b1),
    .ENT(1'b1), .Q0(CF_EN), .Q1(CF_RAW[0]), .Q2(CF_RAW[1]), .Q3(CF_RAW[2]));  // open: RCO
  not not_2 (not_2_out, and_2_out);
  and and_1 (PC_CLK1, CF_EN, PC_CLK);
  Hex_Digit_Display hex_digit_display_1 (.value(PC_REG_L_MON[7:4]));  // open: dp
  and and_2 (and_2_out, SIC_INHIBIT, SIC_RST, CF_EN);
  _74574 u_74574_4 (
    .MONITOR_OUT(out_13), .CLK(S_Y), ._0Q(ACC_IN[0]), ._1Q(ACC_IN[1]), ._2Q(ACC_IN[2]), ._3Q(ACC_IN[3]),
    ._4Q(ACC_IN[4]), ._5Q(ACC_IN[5]), ._6Q(ACC_IN[6]), ._7Q(ACC_IN[7]), .EN(D_Y), ._0D(ACC_IN[0]),
    ._1D(ACC_IN[1]), ._2D(ACC_IN[2]), ._3D(ACC_IN[3]), ._4D(ACC_IN[4]), ._5D(ACC_IN[5]), ._6D(ACC_IN[6]),
    ._7D(ACC_IN[7]));
  _74574 u_74574_5 (
    .MONITOR_OUT(out_13), .CLK(S_Y), ._0Q(A_MEM_L_OUT[0]), ._1Q(A_MEM_L_OUT[1]), ._2Q(A_MEM_L_OUT[2]),
    ._3Q(A_MEM_L_OUT[3]), ._4Q(A_MEM_L_OUT[4]), ._5Q(A_MEM_L_OUT[5]), ._6Q(A_MEM_L_OUT[6]),
    ._7Q(A_MEM_L_OUT[7]), .EN(A_Y), ._0D(ACC_IN[0]), ._1D(ACC_IN[1]), ._2D(ACC_IN[2]), ._3D(ACC_IN[3]),
    ._4D(ACC_IN[4]), ._5D(ACC_IN[5]), ._6D(ACC_IN[6]), ._7D(ACC_IN[7]));
  _74574 u_74574_6 (
    .MONITOR_OUT(out_9), .CLK(S_MEM_U), ._0Q(ACC_IN[0]), ._1Q(ACC_IN[1]), ._2Q(ACC_IN[2]), ._3Q(ACC_IN[3]),
    ._4Q(ACC_IN[4]), ._5Q(ACC_IN[5]), ._6Q(ACC_IN[6]), ._7Q(ACC_IN[7]), .EN(D_MEM_U), ._0D(ACC_IN[0]),
    ._1D(ACC_IN[1]), ._2D(ACC_IN[2]), ._3D(ACC_IN[3]), ._4D(ACC_IN[4]), ._5D(ACC_IN[5]), ._6D(ACC_IN[6]),
    ._7D(ACC_IN[7]));
  _74574 u_74574_7 (
    .MONITOR_OUT(out_9), .CLK(S_MEM_U), ._0Q(A_MEM_L_OUT[0]), ._1Q(A_MEM_L_OUT[1]), ._2Q(A_MEM_L_OUT[2]),
    ._3Q(A_MEM_L_OUT[3]), ._4Q(A_MEM_L_OUT[4]), ._5Q(A_MEM_L_OUT[5]), ._6Q(A_MEM_L_OUT[6]),
    ._7Q(A_MEM_L_OUT[7]), .EN(A_MEM_U), ._0D(ACC_IN[0]), ._1D(ACC_IN[1]), ._2D(ACC_IN[2]), ._3D(ACC_IN[3]),
    ._4D(ACC_IN[4]), ._5D(ACC_IN[5]), ._6D(ACC_IN[6]), ._7D(ACC_IN[7]));
  _74574 u_74574_8 (
    .MONITOR_OUT(PC_REG_U_MON), .CLK(S_PC_U), ._0Q(PC_REG_U_OUT[0]), ._1Q(PC_REG_U_OUT[1]),
    ._2Q(PC_REG_U_OUT[2]), ._3Q(PC_REG_U_OUT[3]), ._4Q(PC_REG_U_OUT[4]), ._5Q(PC_REG_U_OUT[5]),
    ._6Q(PC_REG_U_OUT[6]), ._7Q(PC_REG_U_OUT[7]), .EN(1'b0), ._0D(ACC_IN[0]), ._1D(ACC_IN[1]),
    ._2D(ACC_IN[2]), ._3D(ACC_IN[3]), ._4D(ACC_IN[4]), ._5D(ACC_IN[5]), ._6D(ACC_IN[6]), ._7D(ACC_IN[7]));
  Hex_Digit_Display hex_digit_display_2 (.value(PC_REG_L_MON[3:0]));  // open: dp
  not not_3 (PC_GLOB, and_3_out);
  and and_3 (and_3_out, CF_EN, rom_3_data[0]);
  not not_4 (PC_LOAD, rom_3_data[1]);
  and and_4 (and_4_out, SET_FLAG, D_FL_CARRY, ~INV_FLAG);  // AND_Gate
  and and_5 (and_5_out, SET_FLAG, D_FL_CARRY, INV_FLAG);
  and and_6 (and_6_out, SET_FLAG, D_FL_I, ~INV_FLAG);  // AND_Gate
  and and_7 (and_7_out, SET_FLAG, D_FL_I, INV_FLAG);
  _74574 u_74574_9 (
    .MONITOR_OUT(out_16), .CLK(S_X), ._0Q(ACC_IN[0]), ._1Q(ACC_IN[1]), ._2Q(ACC_IN[2]), ._3Q(ACC_IN[3]),
    ._4Q(ACC_IN[4]), ._5Q(ACC_IN[5]), ._6Q(ACC_IN[6]), ._7Q(ACC_IN[7]), .EN(D_X), ._0D(ACC_IN[0]),
    ._1D(ACC_IN[1]), ._2D(ACC_IN[2]), ._3D(ACC_IN[3]), ._4D(ACC_IN[4]), ._5D(ACC_IN[5]), ._6D(ACC_IN[6]),
    ._7D(ACC_IN[7]));
  _74574 u_74574_10 (
    .MONITOR_OUT(out_16), .CLK(S_X), ._0Q(A_MEM_L_OUT[0]), ._1Q(A_MEM_L_OUT[1]), ._2Q(A_MEM_L_OUT[2]),
    ._3Q(A_MEM_L_OUT[3]), ._4Q(A_MEM_L_OUT[4]), ._5Q(A_MEM_L_OUT[5]), ._6Q(A_MEM_L_OUT[6]),
    ._7Q(A_MEM_L_OUT[7]), .EN(A_X), ._0D(ACC_IN[0]), ._1D(ACC_IN[1]), ._2D(ACC_IN[2]), ._3D(ACC_IN[3]),
    ._4D(ACC_IN[4]), ._5D(ACC_IN[5]), ._6D(ACC_IN[6]), ._7D(ACC_IN[7]));
  not not_5 (not_5_out, REG_SET[3]);
  and and_8 (and_8_out, not_5_out, CF_EN);
  and and_9 (and_9_out, CF_EN, REG_SET[3]);
  not not_6 (not_6_out, MEM_BUS[3]);
  and and_10 (and_10_out, not_6_out, 1'b1);
  and and_11 (and_11_out, 1'b1, MEM_BUS[3]);
  not not_7 (not_7_out, ALU_BUS[3]);
  and and_12 (and_12_out, not_7_out, CF_EN);
  and and_13 (and_13_out, CF_EN, ALU_BUS[3]);
  _74574 u_74574_11 (
    .MONITOR_OUT(out_11), .CLK(S_MEM_L), ._0Q(ACC_IN[0]), ._1Q(ACC_IN[1]), ._2Q(ACC_IN[2]), ._3Q(ACC_IN[3]),
    ._4Q(ACC_IN[4]), ._5Q(ACC_IN[5]), ._6Q(ACC_IN[6]), ._7Q(ACC_IN[7]), .EN(D_MEM_L), ._0D(ACC_IN[0]),
    ._1D(ACC_IN[1]), ._2D(ACC_IN[2]), ._3D(ACC_IN[3]), ._4D(ACC_IN[4]), ._5D(ACC_IN[5]), ._6D(ACC_IN[6]),
    ._7D(ACC_IN[7]));
  _74574 u_74574_12 (
    .MONITOR_OUT(out_11), .CLK(S_MEM_L), ._0Q(A_MEM_L_OUT[0]), ._1Q(A_MEM_L_OUT[1]), ._2Q(A_MEM_L_OUT[2]),
    ._3Q(A_MEM_L_OUT[3]), ._4Q(A_MEM_L_OUT[4]), ._5Q(A_MEM_L_OUT[5]), ._6Q(A_MEM_L_OUT[6]),
    ._7Q(A_MEM_L_OUT[7]), .EN(A_MEM_L), ._0D(ACC_IN[0]), ._1D(ACC_IN[1]), ._2D(ACC_IN[2]), ._3D(ACC_IN[3]),
    ._4D(ACC_IN[4]), ._5D(ACC_IN[5]), ._6D(ACC_IN[6]), ._7D(ACC_IN[7]));
  _74574 u_74574_13 (
    .MONITOR_OUT(NULL_MON), .CLK(CLK), ._0Q(A_MEM_L_OUT[0]), ._1Q(A_MEM_L_OUT[1]), ._2Q(A_MEM_L_OUT[2]),
    ._3Q(A_MEM_L_OUT[3]), ._4Q(A_MEM_L_OUT[4]), ._5Q(A_MEM_L_OUT[5]), ._6Q(A_MEM_L_OUT[6]),
    ._7Q(A_MEM_L_OUT[7]), .EN(A_NULL), ._0D(1'b0), ._1D(1'b0), ._2D(1'b0), ._3D(1'b0), ._4D(1'b0),
    ._5D(1'b0), ._6D(1'b0), ._7D(1'b0));
  not not_8 (not_8_out, INV_FLAG);
  _74112 u_74112_1 (
    .CLK2(not_10_out), .CLK1(not_12_out), .K2(ALU_CARRY), .K1(INTERRUPT), .J2(not_9_out), .J1(not_11_out),
    .PR2(and_4_out), .PR1(and_6_out), .Q2(out_6), .Q1(out_12), .nQ2(n74112_1_nq2), .nQ1(n74112_1_nq1),
    .CLR2(and_5_out), .CLR1(and_7_out));
  not not_9 (not_9_out, ALU_CARRY);
  not not_10 (not_10_out, S_FLAGS);
  not not_11 (not_11_out, INTERRUPT);
  not not_12 (not_12_out, S_FLAGS);
  and and_14 (and_14_out, D_FL_I, not_13_out);
  not not_13 (not_13_out, INV_FLAG);
  and and_15 (and_15_out, INV_FLAG, D_FL_I);
  _74137 u_74137_1 (
    .A0(REG_SET[0]), .A1(REG_SET[1]), .A2(REG_SET[2]), .nLE(CLK), .nE1(1'b0), .nE2(and_8_out),
    .nY1(n74137_1_ny1), .nY2(n74137_1_ny2), .nY3(n74137_1_ny3), .nY4(n74137_1_ny4), .nY5(n74137_1_ny5),
    .nY6(n74137_1_ny6), .nY7(n74137_1_ny7));  // open: nY0
  _74137 u_74137_2 (
    .A0(REG_SET[0]), .A1(REG_SET[1]), .A2(REG_SET[2]), .nLE(CLK), .nE1(1'b0), .nE2(and_9_out),
    .nY0(n74137_2_ny0), .nY1(MEM_WR), .nY2(n74137_2_ny2), .nY3(WR_STACK), .nY4(n74137_2_ny4),
    .nY5(n74137_2_ny5));  // open: nY6, nY7
  not not_14 (ALL_FLAGS, n74137_2_ny5);
  _74137 u_74137_3 (
    .A0(MEM_BUS[0]), .A1(MEM_BUS[1]), .A2(MEM_BUS[2]), .nLE(CLK), .nE1(1'b0), .nE2(and_10_out), .nY0(MEM_EN),
    .nY1(ALT_MEM), .nY2(D_X), .nY3(D_Y), .nY4(D_MEM_U), .nY5(D_MEM_L), .nY6(n74137_3_ny6), .nY7(n74137_3_ny7));
  _74137 u_74137_4 (
    .A0(MEM_BUS[0]), .A1(MEM_BUS[1]), .A2(MEM_BUS[2]), .nLE(CLK), .nE1(1'b0), .nE2(and_11_out), .nY0(D_ALU),
    .nY1(D_ACC), .nY2(D_U_PCO), .nY3(D_L_PCO), .nY4(n74137_4_ny4), .nY5(n74137_4_ny5), .nY6(n74137_4_ny6),
    .nY7(n74137_4_ny7));
  _74137 u_74137_5 (
    .A0(ALU_BUS[0]), .A1(ALU_BUS[1]), .A2(ALU_BUS[2]), .nLE(CLK), .nE1(1'b0), .nE2(and_12_out), .nY0(A_NULL),
    .nY1(A_ACC), .nY2(A_X), .nY3(A_Y), .nY4(A_MEM_U), .nY5(A_MEM_L), .nY6(A_ALU), .nY7(A_MEM));
  _74137 u_74137_6 (
    .A0(ALU_BUS[0]), .A1(ALU_BUS[1]), .A2(ALU_BUS[2]), .nLE(CLK), .nE1(1'b0), .nE2(and_13_out),
    .nY0(n74137_6_ny0), .nY1(n74137_6_ny1), .nY2(D_FLAGS), .nY3(DEC_STACK), .nY4(INC_STACK));  // open: nY5, nY6, nY7
  and and_16 (and_16_out, D_FL_CARRY, not_8_out);
  and and_17 (and_17_out, INV_FLAG, D_FL_CARRY);
  not not_15 (S_ACC, n74137_1_ny1);
  not not_16 (S_X, n74137_1_ny2);
  not not_17 (S_Y, n74137_1_ny3);
  not not_18 (S_MEM_U, n74137_1_ny4);
  not not_19 (S_MEM_L, n74137_1_ny5);
  not not_20 (S_PC_U, n74137_1_ny6);
  not not_21 (S_PC_L, n74137_1_ny7);
  not not_22 (S_ALU, n74137_2_ny0);
  not not_23 (S_MEZZ, n74137_2_ny2);
  not not_24 (S_SP_H, n74137_2_ny4);
  not not_25 (D_FL_OF, n74137_3_ny6);
  not not_26 (D_FL_CARRY, n74137_3_ny7);
  not not_27 (D_FL_I, n74137_4_ny4);
  not not_28 (D_FL_SIGN, n74137_4_ny5);
  not not_29 (D_FL_EC, n74137_4_ny6);
  not not_30 (D_FL_ZC, n74137_4_ny7);
  not not_31 (out_5, n74137_6_ny0);
  Hex_Digit_Display hex_digit_display_3 (.value(ACC_IN[7:4]));  // open: dp
  Hex_Digit_Display hex_digit_display_4 (.value(A_MEM_L_OUT[3:0]));  // open: dp
  Hex_Digit_Display hex_digit_display_5 (.value(A_MEM_L_OUT[7:4]));  // open: dp
  and and_18 (FL_CARRY, and_16_out, out_6);
  and and_19 (nFL_CARRY, and_17_out, n74112_1_nq2);
  and and_20 (FL_I, and_14_out, out_12);
  and and_21 (nFL_I, and_15_out, n74112_1_nq1);
  or or_1 (or_1_out, FL_CARRY, nFL_CARRY, FL_EC, nFL_EC, FL_ZC, nFL_ZC, FL_I, nFL_I);
  not not_32 (SIC_INHIBIT, or_1_out);
  Hex_Digit_Display hex_digit_display_6 (.value(ACC_IN[3:0]));  // open: dp
  not not_33 (not_33_out, out_6);
  and and_22 (ALU_SUB, ~ALU_SEL[0], ALU_SEL[1], ALU_SEL[2], ~ALU_SEL[3]);  // AND_Gate
  and and_23 (ALU_ADD, ALU_SEL[0], ~ALU_SEL[1], ~ALU_SEL[2], ALU_SEL[3]);  // AND_Gate
  or or_2 (S_FLAGS, S_ALU, ALL_FLAGS);
  and and_24 (and_24_out, PC_OUT[15], out_5);
  not not_34 (not_34_out, PC_OUT[15]);
  and and_25 (and_25_out, SET_FLAG, D_FL_EC, ~INV_FLAG);  // AND_Gate
  and and_26 (and_26_out, SET_FLAG, D_FL_EC, INV_FLAG);
  and and_27 (and_27_out, SET_FLAG, D_FL_ZC, ~INV_FLAG);  // AND_Gate
  and and_28 (and_28_out, SET_FLAG, D_FL_ZC, INV_FLAG);
  not not_35 (not_35_out, PC_CLK1);
  and and_29 (and_29_out, not_34_out, out_5);
  _74181 u_74181_1 (
    .S0(ALU_SEL[0]), .S1(ALU_SEL[1]), .S2(ALU_SEL[2]), .S3(ALU_SEL[3]), .Cn(not_33_out), .M(ALU_M),
    .A0(ACC_IN[0]), .B0(A_MEM_L_OUT[0]), .A1(ACC_IN[1]), .B1(A_MEM_L_OUT[1]), .A2(ACC_IN[2]),
    .B2(A_MEM_L_OUT[2]), .A3(ACC_IN[3]), .B3(A_MEM_L_OUT[3]), .F0(out_20[0]), .F1(out_20[1]),
    .A_B(n74181_1_a_b), .F2(out_20[2]), .F3(out_20[3]), .Cn_4(n74181_1_cn_4));  // open: P, G
  _74181 u_74181_2 (
    .S0(ALU_SEL[0]), .S1(ALU_SEL[1]), .S2(ALU_SEL[2]), .S3(ALU_SEL[3]), .Cn(n74181_1_cn_4), .M(ALU_M),
    .A0(ACC_IN[4]), .B0(A_MEM_L_OUT[4]), .A1(ACC_IN[5]), .B1(A_MEM_L_OUT[5]), .A2(ACC_IN[6]),
    .B2(A_MEM_L_OUT[6]), .A3(ACC_IN[7]), .B3(A_MEM_L_OUT[7]), .F0(out_20[4]), .F1(out_20[5]),
    .A_B(n74181_2_a_b), .F2(out_20[6]), .F3(out_20[7]), .Cn_4(n74181_2_cn_4));  // open: P, G
  not not_36 (not_36_out, ALU_AB);
  not not_37 (not_37_out, S_FLAGS);
  not not_38 (not_38_out, INV_FLAG);
  RAM #(.addrWidth(15), .bus("asynch")) ram_1 (
    .addr(PC_OUT[14:0]), .data(MEM_DIRECT), .sel(and_24_out), .ld(MEM_W));  // open: clr
  RAM #(.addrWidth(15), .bus("asynch")) ram_2 (
    .addr(PC_OUT[14:0]), .data(MEM_DIRECT), .sel(and_29_out), .ld(MEM_W));  // open: clr
  _74574 u_74574_14 (
    .MONITOR_OUT(out_18), .CLK(S_MEZZ), ._0Q(MEZZ_OUT[0]), ._1Q(MEZZ_OUT[1]), ._2Q(MEZZ_OUT[2]),
    ._3Q(MEZZ_OUT[3]), ._4Q(MEZZ_OUT[4]), ._5Q(MEZZ_OUT[5]), ._6Q(MEZZ_OUT[6]), ._7Q(MEZZ_OUT[7]), .EN(1'b0),
    ._0D(ACC_IN[0]), ._1D(ACC_IN[1]), ._2D(ACC_IN[2]), ._3D(ACC_IN[3]), ._4D(ACC_IN[4]), ._5D(ACC_IN[5]),
    ._6D(ACC_IN[6]), ._7D(ACC_IN[7]));
  and and_30 (and_30_out, D_FL_EC, not_39_out);
  not not_39 (not_39_out, INV_FLAG);
  and and_31 (and_31_out, INV_FLAG, D_FL_EC);
  _74112 u_74112_2 (
    .CLK2(not_37_out), .CLK1(not_41_out), .K2(ALU_AB), .K1(ALU_ZERO), .J2(not_36_out), .J1(not_40_out),
    .PR2(and_25_out), .PR1(and_27_out), .Q2(out_10), .Q1(out_8), .nQ2(n74112_2_nq2), .nQ1(n74112_2_nq1),
    .CLR2(and_26_out), .CLR1(and_28_out));
  not not_40 (not_40_out, ALU_ZERO);
  not not_41 (not_41_out, S_FLAGS);
  and and_32 (and_32_out, D_FL_ZC, not_38_out);
  and and_33 (and_33_out, INV_FLAG, D_FL_ZC);
  _74245 u_74245_1 (
    .DIR(1'b1), .A0(out_6), .A1(out_7), .A2(out_8), .A3(out_10), .A4(out_15), .A5(out_12), .A6(1'b0),
    .A7(1'b0), .nOE(D_FLAGS), .B0(ACC_IN[0]), .B1(ACC_IN[1]), .B2(ACC_IN[2]), .B3(ACC_IN[3]), .B4(ACC_IN[4]),
    .B5(ACC_IN[5]), .B6(ACC_IN[6]), .B7(ACC_IN[7]));
  xor xor_1 (xor_1_out, PC_GLOB, not_35_out);
  xor xor_2 (xor_2_out, n74163_2_rco, PC_GLOB);
  xor xor_3 (xor_3_out, n74163_3_rco, PC_GLOB);
  xor xor_4 (xor_4_out, n74163_4_rco, PC_GLOB);
  Hex_Digit_Display hex_digit_display_7 (.value(MEM_DIRECT[7:4]));  // open: dp
  _74245 u_74245_2 (
    .DIR(1'b1), .A0(MEM_DIRECT[0]), .A1(MEM_DIRECT[1]), .A2(MEM_DIRECT[2]), .A3(MEM_DIRECT[3]),
    .A4(MEM_DIRECT[4]), .A5(MEM_DIRECT[5]), .A6(MEM_DIRECT[6]), .A7(MEM_DIRECT[7]), .nOE(A_MEM),
    .B0(A_MEM_L_OUT[0]), .B1(A_MEM_L_OUT[1]), .B2(A_MEM_L_OUT[2]), .B3(A_MEM_L_OUT[3]), .B4(A_MEM_L_OUT[4]),
    .B5(A_MEM_L_OUT[5]), .B6(A_MEM_L_OUT[6]), .B7(A_MEM_L_OUT[7]));
  and and_34 (FL_EC, and_30_out, out_10);
  and and_35 (nFL_EC, and_31_out, n74112_2_nq2);
  _74163 u_74163_2 (
    .nLOAD(PC_LOAD), .D0(PC_REG_L_OUT[0]), .D1(PC_REG_L_OUT[1]), .CLK(xor_1_out), .D2(PC_REG_L_OUT[2]),
    .D3(PC_REG_L_OUT[3]), .nCLR(PC_CLR), .ENP(1'b1), .ENT(1'b1), .Q0(PC_RAW_L[0]), .Q1(PC_RAW_L[1]),
    .Q2(PC_RAW_L[2]), .Q3(PC_RAW_L[3]), .RCO(n74163_2_rco));
  _74163 u_74163_3 (
    .nLOAD(PC_LOAD), .D0(PC_REG_L_OUT[4]), .D1(PC_REG_L_OUT[5]), .CLK(xor_2_out), .D2(PC_REG_L_OUT[6]),
    .D3(PC_REG_L_OUT[7]), .nCLR(PC_CLR), .ENP(1'b1), .ENT(1'b1), .Q0(PC_RAW_L[4]), .Q1(PC_RAW_L[5]),
    .Q2(PC_RAW_L[6]), .Q3(PC_RAW_L[7]), .RCO(n74163_3_rco));
  _74163 u_74163_4 (
    .nLOAD(PC_LOAD), .D0(PC_REG_U_OUT[0]), .D1(PC_REG_U_OUT[1]), .CLK(xor_3_out), .D2(PC_REG_U_OUT[2]),
    .D3(PC_REG_U_OUT[3]), .nCLR(PC_CLR), .ENP(1'b1), .ENT(1'b1), .Q0(PC_RAW_U[0]), .Q1(PC_RAW_U[1]),
    .Q2(PC_RAW_U[2]), .Q3(PC_RAW_U[3]), .RCO(n74163_4_rco));
  _74163 u_74163_5 (
    .nLOAD(PC_LOAD), .D0(PC_REG_U_OUT[4]), .D1(PC_REG_U_OUT[5]), .CLK(xor_4_out), .D2(PC_REG_U_OUT[6]),
    .D3(PC_REG_U_OUT[7]), .nCLR(PC_CLR), .ENP(1'b1), .ENT(1'b1), .Q0(PC_RAW_U[4]), .Q1(PC_RAW_U[5]),
    .Q2(PC_RAW_U[6]), .Q3(PC_RAW_U[7]));  // open: RCO
  Hex_Digit_Display hex_digit_display_8 (.value(MEM_DIRECT[3:0]));  // open: dp
  Hex_Digit_Display hex_digit_display_9 (.value(PC_OUT[15:12]));  // open: dp
  Hex_Digit_Display hex_digit_display_10 (.value(out_17[7:4]));  // open: dp
  Hex_Digit_Display hex_digit_display_11 (.value(out_19[7:4]));  // open: dp
  not not_42 (not_42_out, out_5);
  not not_43 (not_43_out, n74181_2_cn_4);
  and and_36 (FL_ZC, and_32_out, out_8);
  and and_37 (nFL_ZC, and_33_out, n74112_2_nq1);
  _74245 u_74245_3 (
    .DIR(1'b1), .A0(ACC_IN[0]), .A1(ACC_IN[1]), .A2(ACC_IN[2]), .A3(ACC_IN[3]), .A4(ACC_IN[4]),
    .A5(ACC_IN[5]), .A6(ACC_IN[6]), .A7(ACC_IN[7]), .nOE(not_44_out), .B0(ALU_CARRY), .B1(in_3),
    .B2(n74245_3_b2), .B3(n74245_3_b3), .B4(in_4), .B5(n74245_3_b5));  // open: B6, B7
  Hex_Digit_Display hex_digit_display_12 (.value(PC_OUT[11:8]));  // open: dp
  Hex_Digit_Display hex_digit_display_13 (.value(PC_OUT[7:4]));  // open: dp
  Hex_Digit_Display hex_digit_display_14 (.value(out_13[7:4]));  // open: dp
  Hex_Digit_Display hex_digit_display_15 (.value(out_17[3:0]));  // open: dp
  Hex_Digit_Display hex_digit_display_16 (.value(out_19[3:0]));  // open: dp
  and and_38 (and_38_out, not_43_out, or_3_out);
  or or_3 (or_3_out, ALU_SUB, ALU_ADD);
  and and_39 (and_39_out, n74181_1_a_b, n74181_2_a_b);
  nor nor_1 (nor_1_out, out_20[0], out_20[1], out_20[2], out_20[3], out_20[4], out_20[5], out_20[6], out_20[7]);
  _74574 u_74574_15 (
    .MONITOR_OUT(out_14), .CLK(S_ALU), ._0Q(ACC_IN[0]), ._1Q(ACC_IN[1]), ._2Q(ACC_IN[2]), ._3Q(ACC_IN[3]),
    ._4Q(ACC_IN[4]), ._5Q(ACC_IN[5]), ._6Q(ACC_IN[6]), ._7Q(ACC_IN[7]), .EN(D_ALU), ._0D(out_20[0]),
    ._1D(out_20[1]), ._2D(out_20[2]), ._3D(out_20[3]), ._4D(out_20[4]), ._5D(out_20[5]), ._6D(out_20[6]),
    ._7D(out_20[7]));
  not not_44 (not_44_out, ALL_FLAGS);
  _74245 u_74245_4 (
    .DIR(1'b1), .A0(PC_RAW_L[0]), .A1(PC_RAW_L[1]), .A2(PC_RAW_L[2]), .A3(PC_RAW_L[3]), .A4(PC_RAW_L[4]),
    .A5(PC_RAW_L[5]), .A6(PC_RAW_L[6]), .A7(PC_RAW_L[7]), .nOE(PC_OE), .B0(PC_OUT[0]), .B1(PC_OUT[1]),
    .B2(PC_OUT[2]), .B3(PC_OUT[3]), .B4(PC_OUT[4]), .B5(PC_OUT[5]), .B6(PC_OUT[6]), .B7(PC_OUT[7]));
  Hex_Digit_Display hex_digit_display_17 (.value(PC_OUT[3:0]));  // open: dp
  _74245 u_74245_5 (
    .DIR(1'b1), .A0(MEM_DIRECT[0]), .A1(MEM_DIRECT[1]), .A2(MEM_DIRECT[2]), .A3(MEM_DIRECT[3]),
    .A4(MEM_DIRECT[4]), .A5(MEM_DIRECT[5]), .A6(MEM_DIRECT[6]), .A7(MEM_DIRECT[7]), .nOE(and_40_out),
    .B0(ACC_IN[0]), .B1(ACC_IN[1]), .B2(ACC_IN[2]), .B3(ACC_IN[3]), .B4(ACC_IN[4]), .B5(ACC_IN[5]),
    .B6(ACC_IN[6]), .B7(ACC_IN[7]));
  and and_40 (and_40_out, ALT_MEM, MEM_EN, DEC_STACK);
  Hex_Digit_Display hex_digit_display_18 (.value(out_13[3:0]));  // open: dp
  Hex_Digit_Display hex_digit_display_19 (.value(out_16[7:4]));  // open: dp
  ROM #(.addrWidth(11)) rom_4 (.addr(PC_OUT[10:0]), .data(MEM_DIRECT), .sel(not_42_out));
  and and_41 (and_41_out, SET_FLAG, D_FL_SIGN, ~INV_FLAG);  // AND_Gate
  and and_42 (and_42_out, SET_FLAG, D_FL_SIGN, INV_FLAG);
  and and_43 (and_43_out, SET_FLAG, D_FL_OF, ~INV_FLAG);  // AND_Gate
  and and_44 (and_44_out, SET_FLAG, D_FL_OF, INV_FLAG);
  _74245 u_74245_6 (
    .DIR(1'b1), .A0(PC_RAW_U[0]), .A1(PC_RAW_U[1]), .A2(PC_RAW_U[2]), .A3(PC_RAW_U[3]), .A4(PC_RAW_U[4]),
    .A5(PC_RAW_U[5]), .A6(PC_RAW_U[6]), .A7(PC_RAW_U[7]), .nOE(PC_OE), .B0(PC_OUT[8]), .B1(PC_OUT[9]),
    .B2(PC_OUT[10]), .B3(PC_OUT[11]), .B4(PC_OUT[12]), .B5(PC_OUT[13]), .B6(PC_OUT[14]), .B7(PC_OUT[15]));
  Hex_Digit_Display hex_digit_display_20 (.value(MEZZ_OUT[3:0]));  // open: dp
  Hex_Digit_Display hex_digit_display_21 (.value(MEZZ_OUT[7:4]));  // open: dp
  Hex_Digit_Display hex_digit_display_22 (.value(out_16[3:0]));  // open: dp
  _74245 u_74245_7 (
    .DIR(1'b1), .A0(and_38_out), .A1(and_39_out), .A2(nor_1_out), .A3(out_20[7]), .nOE(ALL_FLAGS),
    .B0(ALU_CARRY), .B1(ALU_AB), .B2(ALU_ZERO), .B3(in_3));  // open: A4, A5, A6, A7, B4, B5, B6, B7
  not not_45 (PC_CLR, in_2);
  not not_46 (not_46_out, INV_FLAG);
  not not_47 (not_47_out, in_3);
  not not_48 (not_48_out, S_FLAGS);
  not not_49 (not_49_out, INV_FLAG);
  _74245 u_74245_8 (
    .DIR(1'b1), .A0(ACC_IN[0]), .A1(ACC_IN[1]), .A2(ACC_IN[2]), .A3(ACC_IN[3]), .A4(ACC_IN[4]),
    .A5(ACC_IN[5]), .A6(ACC_IN[6]), .A7(ACC_IN[7]), .nOE(MEM_W), .B0(MEM_DIRECT[0]), .B1(MEM_DIRECT[1]),
    .B2(MEM_DIRECT[2]), .B3(MEM_DIRECT[3]), .B4(MEM_DIRECT[4]), .B5(MEM_DIRECT[5]), .B6(MEM_DIRECT[6]),
    .B7(MEM_DIRECT[7]));
  xnor xnor_1 (MEM_W, MEM_WR, WR_STACK);
  and and_45 (and_45_out, D_FL_SIGN, not_46_out);
  and and_46 (and_46_out, INV_FLAG, D_FL_SIGN);
  _74112 u_74112_3 (
    .CLK2(not_48_out), .CLK1(not_51_out), .K2(in_3), .K1(in_4), .J2(not_47_out), .J1(not_50_out),
    .PR2(and_41_out), .PR1(and_43_out), .Q2(out_7), .Q1(out_15), .nQ2(n74112_3_nq2), .nQ1(n74112_3_nq1),
    .CLR2(and_42_out), .CLR1(and_44_out));
  not not_50 (not_50_out, in_4);
  not not_51 (not_51_out, S_FLAGS);
  and and_47 (and_47_out, D_FL_OF, not_49_out);
  and and_48 (and_48_out, INV_FLAG, D_FL_OF);
  _74193 u_74193_1 (
    .CPU(INC_STACK), .CPD(DEC_STACK), .nTCU(n74193_1_ntcu), .nTCD(n74193_1_ntcd), .Q0(out_19[0]),
    .Q1(out_19[1]), .Q2(out_19[2]), .Q3(out_19[3]));  // open: nPL, MR, D0, D1, D2, D3
  _74193 u_74193_2 (
    .CPU(n74193_1_ntcu), .CPD(n74193_1_ntcd), .Q0(out_19[4]), .Q1(out_19[5]), .Q2(out_19[6]), .Q3(out_19[7]));  // open: nPL, MR, nTCU, nTCD, D0, D1, D2, D3
  and and_49 (FL_CARRY, and_45_out, out_7);
  and and_50 (nFL_CARRY, and_46_out, n74112_3_nq2);
  and and_51 (FL_OF, and_47_out, out_15);
  and and_52 (nFL_OF, and_48_out, n74112_3_nq1);
  Hex_Digit_Display hex_digit_display_23 (.value(out_19[7:4]));  // open: dp
  Hex_Digit_Display hex_digit_display_24 (.value(out_19[3:0]));  // open: dp
  _74574 u_74574_16 (
    .MONITOR_OUT(SP_H_MON), .CLK(S_SP_H), ._0Q(SP_H_OUT[0]), ._1Q(SP_H_OUT[1]), ._2Q(SP_H_OUT[2]),
    ._3Q(SP_H_OUT[3]), ._4Q(SP_H_OUT[4]), ._5Q(SP_H_OUT[5]), ._6Q(SP_H_OUT[6]), ._7Q(SP_H_OUT[7]), .EN(1'b0),
    ._0D(ACC_IN[0]), ._1D(ACC_IN[1]), ._2D(ACC_IN[2]), ._3D(ACC_IN[3]), ._4D(ACC_IN[4]), ._5D(ACC_IN[5]),
    ._6D(ACC_IN[6]), ._7D(ACC_IN[7]));
  not not_52 (PC_OE_ALT, xnor_2_out);
  or or_4 (PC_OE, PC_OE_ALT, PC_OE_STACK);
  xnor xnor_2 (xnor_2_out, ALT_MEM, nand_1_out);
  nand nand_1 (nand_1_out, ALU_SUB, SET_FLAG);
  not not_53 (PC_OE_STACK, xnor_3_out);
  and and_53 (and_53_out, SET_FLAG, out_5, ~INV_FLAG);  // AND_Gate
  and and_54 (and_54_out, SET_FLAG, out_5, INV_FLAG);
  and and_55 (and_55_out, SET_FLAG, X, ~INV_FLAG);  // AND_Gate
  and and_56 (and_56_out, SET_FLAG, X, INV_FLAG);
  xnor xnor_3 (xnor_3_out, WR_STACK, DEC_STACK);
  _74245 u_74245_9 (
    .DIR(1'b1), .A0(PC_REG_L_OUT[0]), .A1(PC_REG_L_OUT[1]), .A2(PC_REG_L_OUT[2]), .A3(PC_REG_L_OUT[3]),
    .A4(PC_REG_L_OUT[4]), .A5(PC_REG_L_OUT[5]), .A6(PC_REG_L_OUT[6]), .A7(PC_REG_L_OUT[7]), .nOE(xnor_2_out),
    .B0(PC_OUT[0]), .B1(PC_OUT[1]), .B2(PC_OUT[2]), .B3(PC_OUT[3]), .B4(PC_OUT[4]), .B5(PC_OUT[5]),
    .B6(PC_OUT[6]), .B7(PC_OUT[7]));
  _74245 u_74245_10 (
    .DIR(1'b1), .A0(PC_REG_U_OUT[0]), .A1(PC_REG_U_OUT[1]), .A2(PC_REG_U_OUT[2]), .A3(PC_REG_U_OUT[3]),
    .A4(PC_REG_U_OUT[4]), .A5(PC_REG_U_OUT[5]), .A6(PC_REG_U_OUT[6]), .A7(PC_REG_U_OUT[7]), .nOE(xnor_2_out),
    .B0(PC_OUT[8]), .B1(PC_OUT[9]), .B2(PC_OUT[10]), .B3(PC_OUT[11]), .B4(PC_OUT[12]), .B5(PC_OUT[13]),
    .B6(PC_OUT[14]), .B7(PC_OUT[15]));
  not not_54 (not_54_out, INV_FLAG);
  not not_55 (not_55_out, INV_FLAG);
  _74245 u_74245_11 (
    .DIR(1'b1), .A0(PC_RAW_L[0]), .A1(PC_RAW_L[1]), .A2(PC_RAW_L[2]), .A3(PC_RAW_L[3]), .A4(PC_RAW_L[4]),
    .A5(PC_RAW_L[5]), .A6(PC_RAW_L[6]), .A7(PC_RAW_L[7]), .nOE(D_L_PCO), .B0(ACC_IN[0]), .B1(ACC_IN[1]),
    .B2(ACC_IN[2]), .B3(ACC_IN[3]), .B4(ACC_IN[4]), .B5(ACC_IN[5]), .B6(ACC_IN[6]), .B7(ACC_IN[7]));
  _74245 u_74245_12 (
    .DIR(1'b1), .A0(PC_RAW_U[0]), .A1(PC_RAW_U[1]), .A2(PC_RAW_U[2]), .A3(PC_RAW_U[3]), .A4(PC_RAW_U[4]),
    .A5(PC_RAW_U[5]), .A6(PC_RAW_U[6]), .A7(PC_RAW_U[7]), .nOE(D_U_PCO), .B0(ACC_IN[0]), .B1(ACC_IN[1]),
    .B2(ACC_IN[2]), .B3(ACC_IN[3]), .B4(ACC_IN[4]), .B5(ACC_IN[5]), .B6(ACC_IN[6]), .B7(ACC_IN[7]));
  _74245 u_74245_13 (
    .DIR(1'b1), .A0(out_19[0]), .A1(out_19[1]), .A2(out_19[2]), .A3(out_19[3]), .A4(out_19[4]),
    .A5(out_19[5]), .A6(out_19[6]), .A7(out_19[7]), .nOE(xnor_3_out), .B0(PC_OUT[0]), .B1(PC_OUT[1]),
    .B2(PC_OUT[2]), .B3(PC_OUT[3]), .B4(PC_OUT[4]), .B5(PC_OUT[5]), .B6(PC_OUT[6]), .B7(PC_OUT[7]));
  _74245 u_74245_14 (
    .DIR(1'b1), .A0(SP_H_OUT[0]), .A1(SP_H_OUT[1]), .A2(SP_H_OUT[2]), .A3(SP_H_OUT[3]), .A4(SP_H_OUT[4]),
    .A5(SP_H_OUT[5]), .A6(SP_H_OUT[6]), .A7(SP_H_OUT[7]), .nOE(xnor_3_out), .B0(PC_OUT[8]), .B1(PC_OUT[9]),
    .B2(PC_OUT[10]), .B3(PC_OUT[11]), .B4(PC_OUT[12]), .B5(PC_OUT[13]), .B6(PC_OUT[14]), .B7(PC_OUT[15]));
  and and_57 (and_57_out, out_5, not_54_out);
  and and_58 (and_58_out, INV_FLAG, out_5);
  _74112 u_74112_4 (
    .CLK1(not_57_out), .K1(X), .J1(not_56_out), .PR2(and_53_out), .PR1(and_55_out), .Q2(out_7), .Q1(out_15),
    .nQ2(n74112_4_nq2), .nQ1(n74112_4_nq1), .CLR2(and_54_out), .CLR1(and_56_out));  // open: CLK2, K2, J2
  not not_56 (not_56_out, X);
  not not_57 (not_57_out, S_FLAGS);
  and and_59 (and_59_out, X, not_55_out);
  and and_60 (and_60_out, INV_FLAG, X);
  and and_61 (out_5, and_57_out, out_7);
  and and_62 (nROM_DISABLE, and_58_out, n74112_4_nq2);
  and and_63 (X, and_59_out, out_15);
  and and_64 (nX, and_60_out, n74112_4_nq1);

  // Other names for the same wires on the sheet: SP_L_OUT[7:0] = out_19; ACC_MON[7:0] = out_17; ALU_MON[7:0] = out_14;
  //   ALU_OF = in_4; ALU_RESULT_NOBUF[7:0] = out_20; ALU_SIGN = in_3; FL_CARRY_MON = out_6; FL_EC_MON = out_10;
  //   FL_I_MON = out_12; FL_OF_MON = out_15; FL_SIGN_MON = out_7; FL_ZC_MON = out_8; MEM_L_MON[7:0] = out_11;
  //   MEM_U_MON[7:0] = out_9; RAM_ENABLED = out_5; ROM_DISABLE = out_5; X_MON[7:0] = out_16; Y_MON[7:0] = out_13;
  //   ACC_OUT[7:0] = ACC_IN; ALU_A_IN[7:0] = ACC_IN; ALU_RESULT[7:0] = ACC_IN; FLAGS_IN[7:0] = ACC_IN;
  //   FLAGS_OUT[7:0] = ACC_IN; MEM_L_IN[7:0] = ACC_IN; MEM_L_OUT[7:0] = ACC_IN; MEM_OUT[7:0] = ACC_IN;
  //   MEM_U_IN[7:0] = ACC_IN; MEM_U_OUT[7:0] = ACC_IN; MEZZ_IN[7:0] = ACC_IN; PC_REG_L_IN[7:0] = ACC_IN;
  //   PC_REG_U_IN[7:0] = ACC_IN; PCO_L_OUT[7:0] = ACC_IN; PCO_U_OUT[7:0] = ACC_IN; SP_H_IN[7:0] = ACC_IN;
  //   STACK_OUT[7:0] = ACC_IN; X_IN[7:0] = ACC_IN; X_OUT[7:0] = ACC_IN; Y_IN[7:0] = ACC_IN; Y_OUT[7:0] = ACC_IN;
  //   A_MEM_OUT[7:0] = A_MEM_L_OUT; A_MEM_U_OUT[7:0] = A_MEM_L_OUT; ACC_OUT_A[7:0] = A_MEM_L_OUT;
  //   ALU_NULL_OUT[7:0] = A_MEM_L_OUT; X_OUT_A[7:0] = A_MEM_L_OUT; Y_OUT_A[7:0] = A_MEM_L_OUT

  // Notes on the sheet:
  //   Microcode ROM
  //   contents of rom_1 (hex, n*v repeats v):
  //   11*1a 5*0 60*1a a 7*1a 0 0 14*1a 21*0 6*1a 0 4*1a 0 10*1a 0 0 10*1a 6*0 6*1a 0 5*1a 21*0 4*1a 0 0
  //   4*1a 0 0 4*1a 0 0 4*1a 0 0 5*1a 0 0 17*1a 13*0 1a 20 16 6 16 6 16 6 16 6 16 6 6*0 80 0 80 0 80 0 80
  //   0 80 8 16 4*8 18 16 8 8 8 18 16 8 8 18 16 8 18 16 18 16 4*8 18 16 4*8 18 16 4*8 18 16 4*8 18 16 4*8
  //   20 6 6 16 16 6 6 6 0 0 18 16 5*8 80 16 5*80 21*0 80 16 4*80 0 18 16 16 16 0 5*16 1 2 3 4 5 0 0 16 16
  //   80 80 80 0 0 0 16 d 6*0 c 6*0 1 2 3 4 5 21*0 4*1 0 0 4*2 0 0 4*3 0 0 4*4 0 0 4*5 18 0 0 8 8 18 8 8
  //   18 8 8 9*16 13*0 20 0 7 7 17 7 17 7 17 7 17 7 5*0 10*8 1 17 5*1 17 4*1 17 1 1 1 17 1 1 17 1 17 5*1
  //   17 5*1 17 5*1 17 5*1 17 4*1 0 7 7 17 17 7 7 7 0 0 1 17 5*1 18 17 5*8 21*0 8 17 4*8 0 16 17 17 17 0
  //   5*17 5*30 0 0 17 17 4*20 30 30 17 7 6*0 30 5*b 0 5*20 21*0 4*20 0 0 4*20 0 0 4*20 0 0 4*20 0 0 4*20
  //   1 0 0 8*1 9*17 15*0 4*20 a0 a0 20 20 a0 a0 5*0 1 1 2 2 3 3 5 5 4 4 30 8 5*20 8 4*20 8 20 20 20 8 20
  //   20 8 20 8 5*20 8 5*20 8 5*20 8 5*20 8 4*20 0 20 a0 20 a0 9 9 9 0 0 20 8 5*20 1 80 1 2 3 4 5 21*0 30
  //   80 4*20 0 17 9 9 9 0 9 9 1 2 3 7*0 4 5 6*0 b 6 7*0 5*20 55*0 20 0 0 8*20 9*8 17*0 8*20 5*0 10*20 0 1
  //   5*0 1 4*0 1 0 0 0 1 0 0 1 0 1 5*0 1 5*0 1 5*0 1 5*0 1 5*0 7*20 0 0 0 1 5*0 20 8 5*20 22*0 8 5*0 9 20
  //   20 20 0 5*20 7*0 20 20 6*0 b 20 78*0 9*1 41*0 20 5*0 20 4*0 20 0 0 0 20 0 0 20 0 20 5*0 20 5*0 20
  //   5*0 20 5*0 20 15*0 20 6*0 1 27*0 20 5*0 20 24*0 b 79*0 9*20 108*0 20 58*0 20
  //   contents of rom_2 (hex, n*v repeats v):
  //   258*0 40 0 40 0 40 0 40 0 40 5*0 10*70 1 0 21 31 41 51 2 0 32 42 52 3 0 43 53 4 0 54 5 0 97 0 92 93
  //   94 95 27 0 21 23 24 25 37 0 31 32 34 35 47 0 41 42 43 45 57 0 51 52 53 54 0 40 40 0 0 40 40 40 4*0
  //   90 20 30 40 50 70 0 5*70 21*0 70 0 4*70 20*0 70 c0 60 70 c0 60 0 b 7*0 5*c 0 5*b 21*0 20 30 40 50 0
  //   0 90 30 40 50 0 0 90 20 40 50 0 0 90 20 30 50 0 0 90 20 30 40 1 0 0 21 31 1 21 31 1 21 31 25*0 50 0
  //   50 0 50 0 50 0 50 5*0 90 90 20 20 30 30 50 50 40 40 80 0 5*80 0 4*80 0 80 80 80 0 80 80 0 80 0 5*80
  //   0 5*80 0 5*80 0 5*80 0 4*80 0 50 50 0 0 50 50 50 0 0 80 0 5*80 0 0 90 20 30 40 50 21*0 1 0 21 31 41
  //   51 26*0 c b 7*0 90 20 30 40 50 55*0 80 0 0 8*80 26*0 4*f0 4*e0 5*0 10*80 0 11 5*0 12 4*0 13 0 0 0 14
  //   0 0 15 0 97 5*0 27 5*0 37 5*0 47 5*0 57 5*0 4*70 90 20 30 0 0 0 10 5*0 80 70 5*80 22*0 70 6*0 90 20
  //   30 0 40 50 10 10 10 7*0 10 10 6*0 ac b 78*0 11 12 13 11 12 13 11 12 13 41*0 80 5*0 80 4*0 80 0 0 0
  //   80 0 0 80 0 80 5*0 80 5*0 80 5*0 80 5*0 80 15*0 80 6*0 10 27*0 11 5*0 80 24*0 bc 79*0 9*80 108*0 80
  //   58*0 7a
  //   contents of rom_3 (hex, n*v repeats v):
  //   272*0 10*8 90 0 5*90 0 4*90 0 90 90 90 0 90 90 0 60 0 5*60 0 5*60 0 5*60 0 5*60 0 4*60 10*0 4 0 5*4
  //   8 0 5*8 21*0 8 0 4*8 0 f4 18*0 6*8 69*0 b4 0 0 b4 b4 e4 e4 e4 64 64 64 40*0 f0 0 f0 0 f0 0 f0 0 f0
  //   67*0 c0 0 5*c0 21*0 60 0 4*60 130*0 3 3 24*0 90 5*0 90 4*0 90 0 0 0 90 0 0 90 0 68 5*0 68 5*0 68 5*0
  //   68 5*0 68 9*0 68 68 68 0 0 0 4 6*0 8 27*0 8 6*0 68 68 68 0 68 68 98*0 b4 b4 b4 e4 e4 e4 64 64 64
  //   17*0 8*3 66*0 4*3 13*0 c0 27*0 60 5*0 68 25*0 3 510*0 3
  //   Sub-Instruction Counter (SIC)
  //   Registers
  //   Current State
  //   Carry and Interrupt Flags
  //   Reg Set Decoder
  //   MEM Bus Decoder
  //   ALU Bus Decoder
  //   Generate Signals
  //   Current State
  //   ALU_B_BUS
  //   Current State
  //   Input / Output
  //   Memory Bus
  //   Receive Signals
  //   64kb async RAM
  //   OPCODE_MEZZ
  //   ALU
  //   Hi
  //   Lo
  //   AB and Zero Flags
  //   Mem Value
  //   Program Counter
  //   PC Monitor
  //   RAM ADDR IN
  //   Program ROM
  //   Sign and Overflow Flags
  //   Alternate Memory Driver
  //   PC Reader 
  //   Sign and Overflow Flags
endmodule

module _74137 (
  input  A0,
  input  A1,
  input  A2,
  input  nLE,
  input  nE1,
  input  nE2,
  output nY0,
  output nY1,
  output nY2,
  output nY3,
  output nY4,
  output nY5,
  output nY6,
  output nY7
);

  wire d_ff_1_q, d_ff_1_qn, d_ff_2_q, d_ff_2_qn, d_ff_3_q, d_ff_3_qn, nand_1_out, nand_2_out, nand_3_out,
       nand_4_out, nand_5_out, nand_6_out, nand_7_out, nand_8_out, nor_1_out, nor_2_out, nor_3_out,
       nor_4_out, nor_5_out, nor_6_out, nor_7_out, nor_8_out, nor_9_out, not_1_out, not_2_out, not_3_out,
       not_4_out, not_5_out, not_6_out, not_7_out, not_8_out;

  not not_1 (not_1_out, A0);
  not not_2 (not_2_out, A1);
  not not_3 (not_3_out, A2);
  not not_4 (not_4_out, nLE);
  not not_5 (not_5_out, nE1);
  not not_6 (not_6_out, not_5_out);
  not not_7 (not_7_out, nE2);
  D_Flip_Flop d_ff_1 (.clk(not_4_out), .D(not_1_out), .Q(d_ff_1_q), .Qn(d_ff_1_qn), .en(1'b1));  // open: preset, reset
  D_Flip_Flop d_ff_2 (.clk(not_4_out), .D(not_2_out), .Q(d_ff_2_q), .Qn(d_ff_2_qn), .en(1'b1));  // open: preset, reset
  D_Flip_Flop d_ff_3 (.clk(not_4_out), .D(not_3_out), .Q(d_ff_3_q), .Qn(d_ff_3_qn), .en(1'b1));  // open: preset, reset
  nor nor_1 (nor_1_out, not_6_out, not_7_out);
  nand nand_1 (nand_1_out, d_ff_1_q, d_ff_2_q, d_ff_3_q);
  nand nand_2 (nand_2_out, d_ff_3_q, d_ff_2_q, d_ff_1_qn);
  nand nand_3 (nand_3_out, d_ff_1_q, d_ff_2_qn, d_ff_3_q);
  nand nand_4 (nand_4_out, d_ff_3_q, d_ff_2_qn, d_ff_1_qn);
  nand nand_5 (nand_5_out, d_ff_1_q, d_ff_2_q, d_ff_3_qn);
  nand nand_6 (nand_6_out, d_ff_3_qn, d_ff_2_q, d_ff_1_qn);
  nand nand_7 (nand_7_out, d_ff_1_q, d_ff_2_qn, d_ff_3_qn);
  nand nand_8 (nand_8_out, d_ff_3_qn, d_ff_2_qn, d_ff_1_qn);
  not not_8 (not_8_out, nor_1_out);
  nor nor_2 (nor_2_out, nand_1_out, not_8_out);
  nor nor_3 (nor_3_out, nand_2_out, not_8_out);
  nor nor_4 (nor_4_out, nand_3_out, not_8_out);
  nor nor_5 (nor_5_out, nand_4_out, not_8_out);
  nor nor_6 (nor_6_out, nand_5_out, not_8_out);
  nor nor_7 (nor_7_out, nand_6_out, not_8_out);
  nor nor_8 (nor_8_out, nand_7_out, not_8_out);
  nor nor_9 (nor_9_out, nand_8_out, not_8_out);
  not not_9 (nY0, nor_2_out);
  not not_10 (nY1, nor_3_out);
  not not_11 (nY2, nor_4_out);
  not not_12 (nY3, nor_5_out);
  not not_13 (nY4, nor_6_out);
  not not_14 (nY5, nor_7_out);
  not not_15 (nY6, nor_8_out);
  not not_16 (nY7, nor_9_out);
endmodule

module _74163 (
  input  nLOAD,
  input  D0,
  input  D1,
  input  CLK,
  input  D2,
  input  D3,
  input  nCLR,
  input  ENP,
  input  ENT,
  output Q0,
  output Q1,
  output Q2,
  output Q3,
  output RCO
);

  wire and_1_out, and_2_out, and_3_out, and_4_out, and_5_out, and_6_out, and_7_out, and_8_out, and_9_out,
       and_10_out, and_11_out, and_12_out, nand_1_out, nand_2_out, nand_3_out, nand_4_out, nand_5_out,
       nand_6_out, nand_7_out, nand_8_out, not_1_out, not_2_out, not_3_out, or_1_out, or_2_out, or_3_out,
       or_4_out, or_5_out;

  not not_1 (not_1_out, CLK);
  and and_1 (and_1_out, ENP, ENT);
  not not_2 (not_2_out, nLOAD);
  not not_3 (not_3_out, nCLR);
  or or_1 (or_1_out, not_2_out, not_3_out);
  and and_2 (and_2_out, Q0, and_1_out);
  and and_3 (and_3_out, Q1, Q0, and_1_out);
  and and_4 (and_4_out, Q2, Q1, Q0, and_1_out);
  nand nand_1 (nand_1_out, or_1_out, nand_2_out);
  nand nand_2 (nand_2_out, D0, nCLR, or_1_out);
  nand nand_3 (nand_3_out, or_1_out, nand_4_out);
  nand nand_4 (nand_4_out, D1, nCLR, or_1_out);
  nand nand_5 (nand_5_out, or_1_out, nand_6_out);
  nand nand_6 (nand_6_out, D2, nCLR, or_1_out);
  nand nand_7 (nand_7_out, or_1_out, nand_8_out);
  nand nand_8 (nand_8_out, D3, nCLR, or_1_out);
  and and_5 (and_5_out, nand_1_out, or_2_out);
  or or_2 (or_2_out, and_1_out, or_1_out);
  and and_6 (and_6_out, or_2_out, nand_2_out);
  and and_7 (and_7_out, nand_3_out, or_3_out);
  or or_3 (or_3_out, and_2_out, or_1_out);
  and and_8 (and_8_out, or_3_out, nand_4_out);
  and and_9 (and_9_out, nand_5_out, or_4_out);
  or or_4 (or_4_out, and_3_out, or_1_out);
  and and_10 (and_10_out, or_4_out, nand_6_out);
  and and_11 (and_11_out, nand_7_out, or_5_out);
  or or_5 (or_5_out, and_4_out, or_1_out);
  and and_12 (and_12_out, or_5_out, nand_8_out);
  and and_13 (RCO, Q3, Q2, Q1, Q0, ENT);
  J_K_Flip_Flop j_k_ff_1 (.J(and_5_out), .clk(not_1_out), .K(and_6_out), .Q(Q0), .en(1'b1));  // open: Qn, preset, reset
  J_K_Flip_Flop j_k_ff_2 (.J(and_7_out), .clk(not_1_out), .K(and_8_out), .Q(Q1), .en(1'b1));  // open: Qn, preset, reset
  J_K_Flip_Flop j_k_ff_3 (
    .J(and_9_out), .clk(not_1_out), .K(and_10_out), .Q(Q2), .en(1'b1));  // open: Qn, preset, reset
  J_K_Flip_Flop j_k_ff_4 (
    .J(and_11_out), .clk(not_1_out), .K(and_12_out), .Q(Q3), .en(1'b1));  // open: Qn, preset, reset
endmodule

module _74574 (
  input  CLK,
  input  EN,
  input  _0D,
  input  _1D,
  input  _2D,
  input  _3D,
  input  _4D,
  input  _5D,
  input  _6D,
  input  _7D,
  output _0Q,
  output _1Q,
  output _2Q,
  output _3Q,
  output _4Q,
  output _5Q,
  output _6Q,
  output _7Q,
  output [7:0] MONITOR_OUT
);

  wire not_1_out, not_2_out;

  not not_1 (not_1_out, CLK);
  not not_2 (not_2_out, EN);
  assign _0Q = not_2_out ? MONITOR_OUT[0] : 1'bz;  // Controlled_Buffer controlled_buffer_1
  D_Flip_Flop d_ff_1 (.clk(not_1_out), .D(_0D), .Q(MONITOR_OUT[0]));  // open: Qn, preset, en, reset
  assign _1Q = not_2_out ? MONITOR_OUT[1] : 1'bz;  // Controlled_Buffer controlled_buffer_2
  D_Flip_Flop d_ff_2 (.clk(not_1_out), .D(_1D), .Q(MONITOR_OUT[1]));  // open: Qn, preset, en, reset
  assign _2Q = not_2_out ? MONITOR_OUT[2] : 1'bz;  // Controlled_Buffer controlled_buffer_3
  D_Flip_Flop d_ff_3 (.clk(not_1_out), .D(_2D), .Q(MONITOR_OUT[2]));  // open: Qn, preset, en, reset
  assign _3Q = not_2_out ? MONITOR_OUT[3] : 1'bz;  // Controlled_Buffer controlled_buffer_4
  D_Flip_Flop d_ff_4 (.clk(not_1_out), .D(_3D), .Q(MONITOR_OUT[3]));  // open: Qn, preset, en, reset
  assign _4Q = not_2_out ? MONITOR_OUT[4] : 1'bz;  // Controlled_Buffer controlled_buffer_5
  D_Flip_Flop d_ff_5 (.clk(not_1_out), .D(_4D), .Q(MONITOR_OUT[4]));  // open: Qn, preset, en, reset
  assign _5Q = not_2_out ? MONITOR_OUT[5] : 1'bz;  // Controlled_Buffer controlled_buffer_6
  D_Flip_Flop d_ff_6 (.clk(not_1_out), .D(_5D), .Q(MONITOR_OUT[5]));  // open: Qn, preset, en, reset
  assign _6Q = not_2_out ? MONITOR_OUT[6] : 1'bz;  // Controlled_Buffer controlled_buffer_7
  D_Flip_Flop d_ff_7 (.clk(not_1_out), .D(_6D), .Q(MONITOR_OUT[6]));  // open: Qn, preset, en, reset
  assign _7Q = not_2_out ? MONITOR_OUT[7] : 1'bz;  // Controlled_Buffer controlled_buffer_8
  D_Flip_Flop d_ff_8 (.clk(not_1_out), .D(_7D), .Q(MONITOR_OUT[7]));  // open: Qn, preset, en, reset
endmodule

module _74181 (
  input  Cn,
  input  M,
  input  A0,
  input  B0,
  input  A1,
  input  B1,
  input  A2,
  input  B2,
  input  A3,
  input  B3,
  input  S0,
  input  S1,
  input  S2,
  input  S3,
  output F0,
  output F1,
  output A_B,
  output F2,
  output F3,
  output P,
  output Cn_4,
  output G
);

  wire and_1_out, and_2_out, and_3_out, and_4_out, and_5_out, and_6_out, and_7_out, and_8_out, and_9_out,
       and_11_out, and_12_out, and_13_out, and_14_out, and_15_out, and_16_out, and_17_out, and_18_out,
       and_19_out, and_20_out, and_21_out, and_22_out, and_23_out, and_24_out, and_25_out, and_26_out,
       and_27_out, and_28_out, and_29_out, and_30_out, and_31_out, and_32_out, and_33_out, buffer_1_out,
       buffer_2_out, buffer_3_out, buffer_4_out, buffer_5_out, nand_1_out, nand_3_out, nor_1_out, nor_2_out,
       nor_3_out, nor_4_out, nor_5_out, nor_6_out, nor_7_out, nor_8_out, nor_9_out, nor_10_out, nor_11_out,
       not_1_out, not_2_out, not_3_out, not_4_out, not_5_out, not_6_out, not_7_out, not_8_out, not_9_out;

  not not_1 (not_1_out, M);
  nand nand_1 (nand_1_out, Cn, not_1_out);
  xor xor_1 (F0, nand_1_out, and_2_out);
  buf buffer_1 (buffer_1_out, A0);
  and and_1 (and_1_out, B0, S0);
  nor nor_1 (nor_1_out, buffer_1_out, and_1_out, and_3_out);
  not not_2 (not_2_out, nor_1_out);
  and and_2 (and_2_out, not_2_out, nor_3_out);
  and and_3 (and_3_out, S1, not_3_out);
  and and_4 (and_4_out, not_1_out, nor_1_out);
  not not_3 (not_3_out, B0);
  and and_5 (and_5_out, not_3_out, S2, A0);
  and and_6 (and_6_out, not_1_out, nor_3_out, Cn);
  nor nor_2 (nor_2_out, and_4_out, and_6_out);
  xor xor_2 (F1, nor_2_out, and_8_out);
  and and_7 (and_7_out, A0, B0, S3);
  nor nor_3 (nor_3_out, and_5_out, and_7_out);
  not not_4 (not_4_out, nor_4_out);
  and and_8 (and_8_out, not_4_out, nor_6_out);
  buf buffer_2 (buffer_2_out, A1);
  and and_9 (and_9_out, not_1_out, nor_4_out);
  and and_10 (A_B, F0, F1, F2, F3);
  and and_11 (and_11_out, B1, S0);
  nor nor_4 (nor_4_out, buffer_2_out, and_11_out, and_13_out);
  and and_12 (and_12_out, not_1_out, nor_1_out, nor_6_out);
  nor nor_5 (nor_5_out, and_9_out, and_12_out, and_14_out);
  xor xor_3 (F2, nor_5_out, and_16_out);
  not not_5 (not_5_out, B1);
  and and_13 (and_13_out, S1, not_5_out);
  and and_14 (and_14_out, not_1_out, Cn, nor_3_out, nor_6_out);
  and and_15 (and_15_out, not_5_out, S2, A1);
  nor nor_6 (nor_6_out, and_15_out, and_17_out);
  not not_6 (not_6_out, nor_7_out);
  and and_16 (and_16_out, not_6_out, nor_9_out);
  buf buffer_3 (buffer_3_out, A2);
  and and_17 (and_17_out, A1, S3, B1);
  and and_18 (and_18_out, not_1_out, nor_7_out);
  and and_19 (and_19_out, B2, S0);
  nor nor_7 (nor_7_out, buffer_3_out, and_19_out, and_22_out);
  and and_20 (and_20_out, not_1_out, nor_1_out, nor_6_out, nor_9_out);
  and and_21 (and_21_out, not_1_out, nor_4_out, nor_9_out);
  nor nor_8 (nor_8_out, and_18_out, and_21_out, and_20_out, and_23_out);
  xor xor_4 (F3, nor_8_out, and_25_out);
  and and_22 (and_22_out, S1, not_7_out);
  and and_23 (and_23_out, not_1_out, Cn, nor_3_out, nor_6_out, nor_9_out);
  not not_7 (not_7_out, B2);
  and and_24 (and_24_out, not_7_out, S2, A2);
  nor nor_9 (nor_9_out, and_24_out, and_26_out);
  not not_8 (not_8_out, nor_10_out);
  and and_25 (and_25_out, not_8_out, nor_11_out);
  and and_26 (and_26_out, A2, S3, B2);
  nand nand_2 (P, Cn, nor_6_out, nor_9_out, nor_11_out);
  buf buffer_4 (buffer_4_out, A3);
  and and_27 (and_27_out, B3, S0);
  nor nor_10 (nor_10_out, buffer_4_out, and_27_out, and_28_out);
  nand nand_3 (nand_3_out, Cn, nor_3_out, nor_6_out, nor_9_out, nor_11_out);
  and and_28 (and_28_out, S1, not_9_out);
  and and_29 (and_29_out, nor_1_out, nor_6_out, nor_9_out, nor_11_out);
  or or_1 (Cn_4, ~nand_3_out, ~G);  // OR_Gate
  not not_9 (not_9_out, B3);
  and and_30 (and_30_out, not_9_out, S2, A3);
  and and_31 (and_31_out, nor_4_out, nor_9_out, nor_11_out);
  and and_32 (and_32_out, A3, S3, B3);
  nor nor_11 (nor_11_out, and_30_out, and_32_out);
  buf buffer_5 (buffer_5_out, nor_10_out);
  and and_33 (and_33_out, nor_7_out, nor_11_out);
  nor nor_12 (G, and_29_out, and_31_out, and_33_out, buffer_5_out);
endmodule

module _574_test (
  input  in_1,
  input  in_2,
  input  in_3,
  input  in_4,
  input  in_5,
  input  in_6,
  input  in_7,
  input  in_8,
  input  in_9,
  input  in_10,
  output out_11,
  output out_12,
  output out_13,
  output out_14,
  output out_15,
  output out_16,
  output out_17,
  output out_18,
  output [7:0] out_19
);

  _74574 u_74574_1 (
    .MONITOR_OUT(out_19), .CLK(in_10), ._0Q(out_11), ._1Q(out_12), ._2Q(out_13), ._3Q(out_14), ._4Q(out_15),
    ._5Q(out_16), ._6Q(out_17), ._7Q(out_18), .EN(in_2), ._0D(in_1), ._1D(in_3), ._2D(in_4), ._3D(in_5),
    ._4D(in_6), ._5D(in_7), ._6D(in_8), ._7D(in_9));
endmodule

module _74112 (
  input  CLK2,
  input  K2,
  input  J2,
  input  PR2,
  input  CLR2,
  input  CLK1,
  input  K1,
  input  J1,
  input  PR1,
  input  CLR1,
  output Q2,
  output nQ2,
  output Q1,
  output nQ1
);

  J_K_Flip_Flop j_k_ff_1 (.J(K2), .clk(CLK2), .K(J2), .Q(Q2), .Qn(nQ2), .preset(PR2), .reset(CLR2));  // open: en
  J_K_Flip_Flop j_k_ff_2 (.J(K1), .clk(CLK1), .K(J1), .Q(Q1), .Qn(nQ1), .preset(PR1), .reset(CLR1));  // open: en
endmodule

module _74245 (
  input  DIR,
  input  nOE,
  input  A0,
  input  A1,
  input  A2,
  input  A3,
  input  A4,
  input  A5,
  input  A6,
  input  A7,
  output B0,
  output B1,
  output B2,
  output B3,
  output B4,
  output B5,
  output B6,
  output B7
);

  wire and_1_out, and_2_out;

  and and_1 (and_1_out, DIR, ~nOE);  // AND_Gate
  assign B0 = and_1_out ? A0 : 1'bz;  // Controlled_Buffer controlled_buffer_1
  assign B1 = and_1_out ? A1 : 1'bz;  // Controlled_Buffer controlled_buffer_2
  assign B2 = and_1_out ? A2 : 1'bz;  // Controlled_Buffer controlled_buffer_3
  assign B3 = and_1_out ? A3 : 1'bz;  // Controlled_Buffer controlled_buffer_4
  assign B4 = and_1_out ? A4 : 1'bz;  // Controlled_Buffer controlled_buffer_5
  assign B5 = and_1_out ? A5 : 1'bz;  // Controlled_Buffer controlled_buffer_6
  assign B6 = and_1_out ? A6 : 1'bz;  // Controlled_Buffer controlled_buffer_7
  assign B7 = and_1_out ? A7 : 1'bz;  // Controlled_Buffer controlled_buffer_8
  and and_2 (and_2_out, ~DIR, ~nOE);  // AND_Gate
  assign A0 = and_2_out ? B0 : 1'bz;  // Controlled_Buffer controlled_buffer_9
  assign A1 = and_2_out ? B1 : 1'bz;  // Controlled_Buffer controlled_buffer_10
  assign A2 = and_2_out ? B2 : 1'bz;  // Controlled_Buffer controlled_buffer_11
  assign A3 = and_2_out ? B3 : 1'bz;  // Controlled_Buffer controlled_buffer_12
  assign A4 = and_2_out ? B4 : 1'bz;  // Controlled_Buffer controlled_buffer_13
  assign A5 = and_2_out ? B5 : 1'bz;  // Controlled_Buffer controlled_buffer_14
  assign A6 = and_2_out ? B6 : 1'bz;  // Controlled_Buffer controlled_buffer_15
  assign A7 = and_2_out ? B7 : 1'bz;  // Controlled_Buffer controlled_buffer_16
endmodule

module _74193 (
  input  D0,
  input  D1,
  input  D2,
  input  D3,
  input  nPL,
  input  CPU,
  input  CPD,
  input  MR,
  output nTCU,
  output nTCD,
  output Q0,
  output Q1,
  output Q2,
  output Q3
);

  wire and_1_out, and_2_out, and_3_out, and_4_out, and_5_out, and_6_out, buffer_1_out, buffer_2_out,
       buffer_3_out, buffer_5_out, buffer_7_out, buffer_9_out, nand_1_out, nand_2_out, nand_3_out,
       nand_4_out, nand_5_out, nand_6_out, nand_7_out, nand_8_out, nand_9_out, nand_10_out, nor_1_out,
       nor_2_out, nor_3_out, nor_4_out, not_1_out, not_2_out, not_3_out, not_4_out, not_5_out, not_6_out,
       not_7_out, not_8_out, or_1_out, or_2_out, or_3_out, or_4_out, t_ff_1_q, t_ff_1_qn, t_ff_2_q,
       t_ff_2_qn, t_ff_3_q, t_ff_3_qn, t_ff_4_q, t_ff_4_qn;

  not not_1 (not_1_out, nPL);
  not not_2 (not_2_out, CPU);
  buf buffer_1 (buffer_1_out, not_2_out);
  buf buffer_2 (buffer_2_out, not_3_out);
  not not_3 (not_3_out, CPD);
  not not_4 (not_4_out, MR);
  nand nand_1 (nand_1_out, not_1_out, not_4_out, buffer_3_out);
  not not_5 (not_5_out, nand_1_out);
  nor nor_1 (nor_1_out, buffer_1_out, buffer_2_out);
  buf buffer_3 (buffer_3_out, D0);
  nand nand_2 (nand_2_out, nand_1_out, not_1_out);
  T_Flip_Flop t_ff_1 (
    .clk(nor_1_out), .T(1'b1), .Q(t_ff_1_q), .Qn(t_ff_1_qn), .preset(not_5_out), .reset(or_1_out));  // open: en
  or or_1 (or_1_out, ~not_4_out, ~nand_2_out);  // OR_Gate
  buf buffer_4 (Q0, t_ff_1_q);
  and and_1 (and_1_out, not_2_out, t_ff_1_q);
  and and_2 (and_2_out, t_ff_1_qn, not_3_out);
  buf buffer_5 (buffer_5_out, D1);
  nand nand_3 (nand_3_out, not_1_out, not_4_out, buffer_5_out);
  not not_6 (not_6_out, nand_3_out);
  T_Flip_Flop t_ff_2 (
    .clk(nor_2_out), .T(1'b1), .Q(t_ff_2_q), .Qn(t_ff_2_qn), .preset(not_6_out), .reset(or_2_out));  // open: en
  nor nor_2 (nor_2_out, and_1_out, and_2_out);
  or or_2 (or_2_out, ~not_4_out, ~nand_4_out);  // OR_Gate
  nand nand_4 (nand_4_out, nand_3_out, not_1_out);
  buf buffer_6 (Q1, t_ff_2_q);
  and and_3 (and_3_out, not_2_out, t_ff_1_q, t_ff_2_q);
  nor nor_3 (nor_3_out, and_3_out, and_4_out);
  and and_4 (and_4_out, t_ff_2_qn, t_ff_1_qn, not_3_out);
  buf buffer_7 (buffer_7_out, D2);
  nand nand_5 (nand_5_out, not_1_out, not_4_out, buffer_7_out);
  nand nand_6 (nand_6_out, nand_5_out, not_1_out);
  not not_7 (not_7_out, nand_5_out);
  T_Flip_Flop t_ff_3 (
    .clk(nor_3_out), .T(1'b1), .Q(t_ff_3_q), .Qn(t_ff_3_qn), .preset(not_7_out), .reset(or_3_out));  // open: en
  or or_3 (or_3_out, ~not_4_out, ~nand_6_out);  // OR_Gate
  buf buffer_8 (Q2, t_ff_3_q);
  and and_5 (and_5_out, not_2_out, t_ff_1_q, t_ff_2_q, t_ff_3_q);
  and and_6 (and_6_out, t_ff_3_qn, t_ff_2_qn, t_ff_1_qn, not_3_out);
  nor nor_4 (nor_4_out, and_5_out, and_6_out);
  buf buffer_9 (buffer_9_out, D3);
  nand nand_7 (nand_7_out, nand_8_out, not_1_out);
  nand nand_8 (nand_8_out, not_1_out, not_4_out, buffer_9_out);
  not not_8 (not_8_out, nand_8_out);
  T_Flip_Flop t_ff_4 (
    .clk(nor_4_out), .T(1'b1), .Q(t_ff_4_q), .Qn(t_ff_4_qn), .preset(not_8_out), .reset(or_4_out));  // open: en
  or or_4 (or_4_out, ~not_4_out, ~nand_7_out);  // OR_Gate
  nand nand_9 (nand_9_out, not_2_out, t_ff_1_q, t_ff_2_q, t_ff_3_q, t_ff_4_q);
  nand nand_10 (nand_10_out, t_ff_4_qn, t_ff_3_qn, t_ff_2_qn, t_ff_1_qn, not_3_out);
  buf buffer_10 (Q3, t_ff_4_q);
  buf buffer_11 (nTCU, nand_9_out);
  buf buffer_12 (nTCD, nand_10_out);
endmodule
